# Fritzing sketch vestiar (saved by Fritzing 1.0.5)

parts:
  Mod1 = Amica NodeMCU DEVKIT 1.0
  R1 = Resistor [tolerance=±5% power=0.25W resistance=10k package=THT]
  R2 = Resistor [tolerance=±5% power=0.25W resistance=10k package=THT]
  U1 = 2-Channel 5v Relay Shield [package=relay-2ch5v10a]
  JACK1 = 2.1mm Barrel Jack with Terminal Block
  kEYPAD_MATRICIAL_1 = KEYPAD 4x3
  R3 = Resistor [tolerance=±5% power=0.25W resistance=10k package=THT]
  Ghercon = Pushbutton [package=THT]

nets:
  N1: Mod1.pin1, Mod1.pin_26, R1.Pin_1, R2.Pin_1, R3.Pin_1
  N2: Mod1.pin7, kEYPAD_MATRICIAL_1.arrow4
  N3: Mod1.pin_9, Mod1.pin_25, Mod1.pin_29, U1.GND, JACK1.NEG, kEYPAD_MATRICIAL_1.col1
  N4: Mod1.pin_11, U1.IN2
  N5: Mod1.pin_13, R3.Pin_0, Ghercon.leg0
  N6: Mod1.pin_15, U1.IN1
  N7: Mod1.pin_30, U1.VCC

custom parts:
  2-Channel 5v Relay Shield: 2 Channel 5v Relay Shield w. 2x SPD-06VDC-SD-C
  KEYPAD 4x3: KEYPAD matricial de 12 botones, 4 filas x 3 columnas
